# Fritzing sketch Final Drawing (saved by Fritzing 0.9.10b)

parts:
  BATT2 = LiPoly Battery (1300mAh)  # not connected
  Adafruit#2 = Adafruit DRV2605L Haptic Motor Controller - STEMMA QT [part_number=2305]
  PCA3 = Adafruit PCA9548 8-Channel STEMMA QT / Qwiic I2C Multiplexer [part_number=5626]
  MOTOR2 = Vibration Motor  # not connected
  Adafruit#3 = Adafruit DRV2605L Haptic Motor Controller - STEMMA QT [part_number=2305]
  Adafruit#4 = Adafruit DRV2605L Haptic Motor Controller - STEMMA QT [part_number=2305]
  Adafruit#5 = Adafruit DRV2605L Haptic Motor Controller - STEMMA QT [part_number=2305]

nets:
  GND: Adafruit#2.GND, PCA3.GND, Adafruit#3.GND, Adafruit#4.GND, Adafruit#5.GND
  VCC: Adafruit#2.VCC, PCA3.VCCIO, Adafruit#3.VCC, Adafruit#4.VCC, Adafruit#5.VCC
  N1: Adafruit#2.SDA, PCA3.4SDA
  N2: Adafruit#2.SCL, PCA3.4SCL
  N3: PCA3.5SDA, Adafruit#3.SDA
  N4: PCA3.5SCL, Adafruit#3.SCL
  N5: PCA3.6SDA, Adafruit#4.SDA
  N6: PCA3.6SCL, Adafruit#4.SCL
  N7: PCA3.7SDA, Adafruit#5.SDA
  N8: PCA3.7SCL, Adafruit#5.SCL

custom parts:
  LiPoly Battery (1300mAh): Lithium Ion Polymer Battery (1300mAh)
  Adafruit DRV2605L Haptic Motor Controller - STEMMA QT: The DRV2605 from TI is a fancy little motor driver. Rather than controlling a stepper motor or DC motor, its designed specifically for controlling haptic motors - buzzers and vibration motors. Normally one would just turn those kinds of motors on and off, but this driver has the ability to have various effects when driving a vibe motor. For example, ramping the vibration level up and down,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
  Adafruit PCA9548 8-Channel STEMMA QT / Qwiic I2C Multiplexer: You just found the perfect I2C sensor, available in a handy chainable Qwiic, or STEMMA QT package, and you want to wire up two or three or more of them to your microcontroller when you realize "Uh oh, this chip has a fixed I2C address, and from what I know about I2C, you cannot have two devices with the same address on the same SDA/SCL pins!" Are you out of luck? You would be, if you didn't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
  Vibration Motor: An eccentric vibration motor!
