# Fritzing sketch Initial Testing (saved by Fritzing 0.9.10b)

parts:
  MOTOR1 = Vibration Motor
  PCA2 = Adafruit PCA9548 8-Channel STEMMA QT / Qwiic I2C Multiplexer [part_number=5626]
  BATT1 = LiPoly Battery (1300mAh)
  U1 = ESP32-38PinWide [part_number=ESP32-38PinWide]
  Adafruit#1 = Adafruit DRV2605L Haptic Motor Controller - STEMMA QT [part_number=2305]

nets:
  N1: MOTOR1.POS, Adafruit#1.OUT-
  N2: MOTOR1.NEG, Adafruit#1.OUT+
  GND: PCA2.GND, U1.GPIO3, Adafruit#1.GND
  N3: PCA2.VCC, BATT1.positive, U1.3.3
  N4: PCA2.SDA, U1.GPIO21
  N5: PCA2.SCL, U1.GPIO22
  N6: PCA2.VCCIO, Adafruit#1.VCC
  N7: PCA2.4SDA, Adafruit#1.SDA
  N8: PCA2.4SCL, Adafruit#1.SCL
  N9: BATT1.negative, U1.GND

custom parts:
  Vibration Motor: An eccentric vibration motor!
  Adafruit PCA9548 8-Channel STEMMA QT / Qwiic I2C Multiplexer: You just found the perfect I2C sensor, available in a handy chainable Qwiic, or STEMMA QT package, and you want to wire up two or three or more of them to your microcontroller when you realize "Uh oh, this chip has a fixed I2C address, and from what I know about I2C, you cannot have two devices with the same address on the same SDA/SCL pins!" Are you out of luck? You would be, if you didn't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
  LiPoly Battery (1300mAh): Lithium Ion Polymer Battery (1300mAh)
  ESP32-38PinWide: Generic 38-Pin ESP32 with wide format (only access to one side of pins on a breadboard) based on Stephen Lilley's HiLetgo ESP-WROOM-32 ESP32 ESP-32S Development Board.
  Adafruit DRV2605L Haptic Motor Controller - STEMMA QT: The DRV2605 from TI is a fancy little motor driver. Rather than controlling a stepper motor or DC motor, its designed specifically for controlling haptic motors - buzzers and vibration motors. Normally one would just turn those kinds of motors on and off, but this driver has the ability to have various effects when driving a vibe motor. For example, ramping the vibration level up and down,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
