# Fritzing sketch Final Drawing (saved by Fritzing 0.9.10b)

parts:
  Adafruit#2 = Adafruit DRV2605L Haptic Motor Controller - STEMMA QT [part_number=2305]
  PCA3 = Adafruit PCA9548 8-Channel STEMMA QT / Qwiic I2C Multiplexer [part_number=5626]
  MOTOR2 = Vibration Motor
  Adafruit#3 = Adafruit DRV2605L Haptic Motor Controller - STEMMA QT [part_number=2305]
  Adafruit#4 = Adafruit DRV2605L Haptic Motor Controller - STEMMA QT [part_number=2305]
  Adafruit#5 = Adafruit DRV2605L Haptic Motor Controller - STEMMA QT [part_number=2305]
  Adafruit#6 = Adafruit DRV2605L Haptic Motor Controller - STEMMA QT [part_number=2305]
  Adafruit#7 = Adafruit DRV2605L Haptic Motor Controller - STEMMA QT [part_number=2305]
  Adafruit#8 = Adafruit DRV2605L Haptic Motor Controller - STEMMA QT [part_number=2305]
  Adafruit#9 = Adafruit DRV2605L Haptic Motor Controller - STEMMA QT [part_number=2305]
  MOTOR3 = Vibration Motor
  MOTOR4 = Vibration Motor
  MOTOR5 = Vibration Motor
  MOTOR6 = Vibration Motor
  MOTOR7 = Vibration Motor
  MOTOR8 = Vibration Motor
  MOTOR9 = Vibration Motor
  元件1 = Adafruit QT Py ESP32-S3 [part_number=5426]
  元件2 = Adafruit LiPoly Charger BFF for QT Py [part_number="Adafruit #5397"]
  元件4 = Adafruit BNO085 9-DOF Orientation IMU Fusion [part_number="Addfruit #4754"]
  BATT2 = LiPoly Battery (1300mAh)

nets:
  GND: Adafruit#2.GND, PCA3.GND, Adafruit#3.GND, Adafruit#4.GND, Adafruit#5.GND, Adafruit#6.GND, Adafruit#7.GND, Adafruit#8.GND, Adafruit#9.GND, 元件1.GND, 元件2.GND, 元件4.GND, BATT2.negative
  VCC: Adafruit#2.VCC, PCA3.VCCIO, Adafruit#3.VCC, Adafruit#4.VCC, Adafruit#5.VCC, Adafruit#6.VCC, Adafruit#7.VCC, Adafruit#8.VCC, Adafruit#9.VCC
  N1: Adafruit#2.SDA, PCA3.4SDA
  N2: Adafruit#2.SCL, PCA3.4SCL
  N3: Adafruit#2.OUT+, MOTOR2.POS
  N4: Adafruit#2.OUT-, MOTOR2.NEG
  N5: PCA3.0SDA, Adafruit#6.SDA
  N6: PCA3.0SCL, Adafruit#6.SCL
  N7: PCA3.1SDA, Adafruit#7.SDA
  N8: PCA3.1SCL, Adafruit#7.SCL
  VCC_2: PCA3.VCC, 元件1.3.3V, 元件2.5#35, 元件4.VCC
  N9: PCA3.SDA, 元件1.SDA1, 元件4.SDA/MISO/TX
  N10: PCA3.SCL, 元件1.SCL1, 元件4.SCL/SCK/RX
  N11: PCA3.2SDA, Adafruit#8.SDA
  N12: PCA3.2SCL, Adafruit#8.SCL
  N13: PCA3.3SDA, Adafruit#9.SDA
  N14: PCA3.3SCL, Adafruit#9.SCL
  N15: PCA3.5SDA, Adafruit#3.SDA
  N16: PCA3.5SCL, Adafruit#3.SCL
  N17: PCA3.6SDA, Adafruit#4.SDA
  N18: PCA3.6SCL, Adafruit#4.SCL
  N19: PCA3.7SDA, Adafruit#5.SDA
  N20: PCA3.7SCL, Adafruit#5.SCL
  N21: Adafruit#3.OUT+, MOTOR3.POS
  N22: Adafruit#3.OUT-, MOTOR3.NEG
  N23: Adafruit#4.OUT+, MOTOR5.POS
  N24: Adafruit#4.OUT-, MOTOR5.NEG
  N25: Adafruit#5.OUT+, MOTOR4.POS
  N26: Adafruit#5.OUT-, MOTOR4.NEG
  N27: Adafruit#6.OUT+, MOTOR7.POS
  N28: Adafruit#6.OUT-, MOTOR7.NEG
  N29: Adafruit#7.OUT+, MOTOR6.POS
  N30: Adafruit#7.OUT-, MOTOR6.NEG
  N31: Adafruit#8.OUT+, MOTOR8.POS
  N32: Adafruit#8.OUT-, MOTOR8.NEG
  N33: Adafruit#9.OUT+, MOTOR9.POS
  N34: Adafruit#9.OUT-, MOTOR9.NEG
  N35: 元件1.A0, 元件2.1#13
  N36: 元件1.A1, 元件2.2#15
  N37: 元件1.A2, 元件2.A2
  N38: 元件1.A3, 元件2.4#19
  N39: 元件1.SDA, 元件2.5#21
  N40: 元件1.SCL, 元件2.6
  N41: 元件1.TX, 元件2.7
  N42: 元件1.RX, 元件2.1#27
  N43: 元件1.SCK, 元件2.2#29
  N44: 元件1.MISO, 元件2.3
  N45: 元件1.MOSI, 元件2.4#33
  +5V: 元件1.+5V, 元件2.+5V
  N46: 元件2.VBAT, BATT2.positive

notes:
  [ME 327 Final Drawing]

custom parts:
  Adafruit DRV2605L Haptic Motor Controller - STEMMA QT: The DRV2605 from TI is a fancy little motor driver. Rather than controlling a stepper motor or DC motor, its designed specifically for controlling haptic motors - buzzers and vibration motors. Normally one would just turn those kinds of motors on and off, but this driver has the ability to have various effects when driving a vibe motor. For example, ramping the vibration level up and down,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
  Adafruit PCA9548 8-Channel STEMMA QT / Qwiic I2C Multiplexer: You just found the perfect I2C sensor, available in a handy chainable Qwiic, or STEMMA QT package, and you want to wire up two or three or more of them to your microcontroller when you realize "Uh oh, this chip has a fixed I2C address, and from what I know about I2C, you cannot have two devices with the same address on the same SDA/SCL pins!" Are you out of luck? You would be, if you didn't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
  Vibration Motor: An eccentric vibration motor!
  Adafruit QT Py ESP32-S3: The ESP32-S3 has arrived in QT Py format - and what a great way to get started with this powerful new chip from Espressif! With dual 240 MHz cores, WiFi and BLE support, and native USB, this QT Py is great for powering your IoT projects. The ESP32-S3 is a highly-integrated, low-power, 2.4 GHz Wi-Fi System-on-Chip (SoC) solution that now has WiFi and BLE support, built-in native USB as well as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
  Adafruit LiPoly Charger BFF for QT Py: Is your QT Py all alone, lacking a friend to travel the wide world with? When you were a kid you may have learned about the "buddy" system, well this product is kinda like that! A board that will watch your QT Py's back and give it the power and support to wander out past your USB port. This little lipo charger is designed to fit onto the back of any QT Py board, and make it easy for portable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
  LiPoly Battery (1300mAh): Lithium Ion Polymer Battery (1300mAh)
