# Fritzing sketch Initial Testing (saved by Fritzing 0.9.10b)

parts:
  BATT1 = LiPoly Battery (1300mAh)
  Adafruit#9 = Adafruit DRV2605L Haptic Motor Controller - STEMMA QT [part_number=2305]
  MOTOR8 = Vibration Motor
  PCA4 = Adafruit PCA9548 8-Channel STEMMA QT / Qwiic I2C Multiplexer [part_number=5626]
  U2 = ESP32-38PinWide [part_number=ESP32-38PinWide]

nets:
  N1: BATT1.positive, PCA4.VCC, U2.3.3
  GND: BATT1.negative, Adafruit#9.GND, PCA4.GND, U2.GND
  N2: Adafruit#9.VCC, PCA4.VCCIO
  N3: Adafruit#9.SDA, PCA4.4SDA
  N4: Adafruit#9.SCL, PCA4.4SCL
  N5: Adafruit#9.OUT+, MOTOR8.POS
  N6: Adafruit#9.OUT-, MOTOR8.NEG
  N7: PCA4.SDA, U2.GPIO21
  N8: PCA4.SCL, U2.GPIO22

notes:
  Initial Testing Drawing

custom parts:
  LiPoly Battery (1300mAh): Lithium Ion Polymer Battery (1300mAh)
  Adafruit DRV2605L Haptic Motor Controller - STEMMA QT: The DRV2605 from TI is a fancy little motor driver. Rather than controlling a stepper motor or DC motor, its designed specifically for controlling haptic motors - buzzers and vibration motors. Normally one would just turn those kinds of motors on and off, but this driver has the ability to have various effects when driving a vibe motor. For example, ramping the vibration level up and down,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
  Vibration Motor: An eccentric vibration motor!
  Adafruit PCA9548 8-Channel STEMMA QT / Qwiic I2C Multiplexer: You just found the perfect I2C sensor, available in a handy chainable Qwiic, or STEMMA QT package, and you want to wire up two or three or more of them to your microcontroller when you realize "Uh oh, this chip has a fixed I2C address, and from what I know about I2C, you cannot have two devices with the same address on the same SDA/SCL pins!" Are you out of luck? You would be, if you didn't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
  ESP32-38PinWide: Generic 38-Pin ESP32 with wide format (only access to one side of pins on a breadboard) based on Stephen Lilley's HiLetgo ESP-WROOM-32 ESP32 ESP-32S Development Board.
